# Fritzing sketch 5ledladder (saved by Fritzing 0.9.3b)
breadboards: 2

parts:
  Part1 = Arduino Uno (Rev3)
  LED1 = LED - 5mm [color="Yellow (595nm)" package="5 mm [THT]"]
  LED2 = LED - 5mm [color="Red (633nm)" package="5 mm [THT]"]
  LED3 = LED - 5mm [color="Green (565nm)" package="5 mm [THT]"]
  LED4 = LED - 5mm [color="Blue (430nm)" package="5 mm [THT]"]
  LED5 = LED - 5mm [color="Infrared (940nm)" package="5 mm [THT]"]
  R1 = Resistor [tolerance=±5% resistance=220 package=THT]
  R2 = Resistor [tolerance=±5% resistance=220 package=THT]
  R3 = Resistor [tolerance=±5% resistance=220 package=THT]
  R4 = Resistor [tolerance=±5% resistance=220 package=THT]
  R5 = Resistor [tolerance=±5% resistance=220 package=THT]
  J1 = Piezo Speaker
  Part2 = Arduino Mega 2560 (Rev3)
  R6 = Resistor [tolerance=±5% resistance=560 package=THT]
  R7 = Resistor [tolerance=±5% resistance=560 package=THT]
  R8 = Resistor [tolerance=±5% resistance=560 package=THT]
  LED6 = RGB LED (com. cathode, rgb) [package="5 mm [THT]"]
  R9 = Photocell (LDR) [package=THT]
  R10 = Resistor [tolerance=±5% resistance=10k package=THT]
  J2 = Infrared Proximity Sensor  # not connected
  LED7 = LED - 5mm [color="Red (633nm)" package="5 mm [THT]"]  # not connected
  R11 = Resistor [tolerance=±5% resistance=220 package=THT]  # not connected

nets:
  N1: Part1.A1, LED5.anode, R5.Pin_0
  N2: Part1.A2, LED4.anode, R4.Pin_0
  N3: Part1.A3, LED3.anode, R2.Pin_0
  N4: Part1.A4/SDA, LED1.anode, R3.Pin_0
  N5: Part1.A5/SCL, LED2.anode, R1.Pin_0
  N6: Part1.D9_PWM, R4.Pin_1
  N7: Part1.D10_PWM/SS, R5.Pin_1
  N8: Part1.D13/SCK, J1.pin2
  N9: Part1.GND, LED1.cathode, LED2.cathode, LED3.cathode, LED4.cathode, LED5.cathode, J1.pin1
  N10: Part1.D3_PWM, R1.Pin_1
  N11: Part1.D5_PWM, R3.Pin_1
  N12: Part1.D6_PWM, R2.Pin_1
  N13: Part2.A0, R9.pin_0, R10.Pin_0
  N14: Part2.GND, LED6.common_cathode, R10.Pin_1
  N15: Part2.D11_PWM, R6.Pin_0
  N16: Part2.D10_PWM, R7.Pin_0
  N17: Part2.D9_PWM, R8.Pin_0
  N18: Part2.3V3, R9.pin_1
  N19: R6.Pin_1, LED6.red_anode
  N20: R7.Pin_1, LED6.green_anode
  N21: R8.Pin_1, LED6.blue_anode
