# Fritzing sketch BlinkingLED (saved by Fritzing 0.9.3b)
breadboards: 1

parts:
  Part1 = Arduino Uno (Rev3)
  R1 = Resistor [tolerance=±5% resistance=220 package=THT]
  R2 = Resistor [tolerance=±5% resistance=220 package=THT]
  LED2 = LED - 5mm [color="Red (633nm)" package="5 mm [THT]"]
  LED3 = LED - 5mm [color="Red (633nm)" package="5 mm [THT]"]

nets:
  N1: Part1.D8, LED3.anode
  N2: Part1.D13/SCK, LED2.anode
  N3: Part1.GND, R1.Pin_0, R2.Pin_0
  N4: R1.Pin_1, LED3.cathode
  N5: R2.Pin_1, LED2.cathode

notes:
  Tanner Helms
  V I R P
  R1 3.03 9.1mA 332 27
  LED1 1.87 9.1mA 202 16
  T1 4.9 9.1mA 534 44
  R2 2.8 9.2mA 304 25
  LED2 1.97 9.2mA 214 18
  T2 4.77 9.2mA 518 43
