# Fritzing sketch Untitled Sketch (saved by Fritzing 0.9.3b)
breadboards: 1

parts:
  Part1 = Arduino Uno (Rev3)
  R1 = Photocell (LDR) [package=THT]
  R2 = Resistor [tolerance=±5% resistance=220 package=THT]
  S1 = Pushbutton [package="[THT]"]
  J1 = Piezo Speaker

nets:
  N1: Part1.A0, R1.pin_1, R2.Pin_0
  N2: Part1.GND, R2.Pin_1, J1.pin1
  N3: Part1.D3_PWM, J1.pin2
  N4: Part1.5V, S1.Pin_3, S1.Pin_4
  N5: R1.pin_0, S1.Pin_1, S1.Pin_2
