# Fritzing sketch colorFading (saved by Fritzing 0.9.3b)
breadboards: 1

parts:
  Part1 = Arduino Uno (Rev3)
  R6 = Resistor [tolerance=±5% resistance=220 package=THT]
  R7 = Resistor [tolerance=±5% resistance=220 package=THT]
  R8 = Resistor [tolerance=±5% resistance=220 package=THT]
  R9 = Resistor [tolerance=±5% resistance=220 package=THT]
  R10 = Resistor [tolerance=±5% resistance=220 package=THT]
  LED6 = LED - 5mm [color="Red (633nm)" package="5 mm [THT]"]
  LED7 = LED - 5mm [color="Yellow (595nm)" package="5 mm [THT]"]
  LED8 = LED - 5mm [color="Green (565nm)" package="5 mm [THT]"]
  LED9 = LED - 5mm [color="Blue (430nm)" package="5 mm [THT]"]
  LED10 = LED - 5mm [color="Infrared (850nm)" package="5 mm [THT]"]

nets:
  N1: Part1.D9_PWM, R9.Pin_1
  N2: Part1.D10_PWM/SS, R7.Pin_1
  N3: Part1.D11_PWM/MOSI, R10.Pin_1
  N4: Part1.D5_PWM, R8.Pin_1
  N5: Part1.D6_PWM, LED7.cathode
  N6: R6.Pin_0, LED7.anode
  N7: R7.Pin_0, LED9.anode
  N8: R8.Pin_0, LED6.anode
  N9: R9.Pin_0, LED8.anode
  N10: R10.Pin_0, LED10.anode
