# Fritzing sketch opamp (saved by Fritzing 0.9.3b)
breadboards: 1

parts:
  Part1 = Arduino Uno (Rev3)
  U1 = LM 358 Dual Op-Amp [package="DIP8 [THT]"]
  R1 = Photocell (LDR) [package=THT]
  R2 = Resistor [tolerance=±5% resistance=1k package=THT]
  R3 = Resistor [tolerance=±5% resistance=1k package=THT]
  R4 = Resistor [tolerance=±5% resistance=1k package=THT]
  R5 = Resistor [tolerance=±5% resistance=220 package=THT]
  R6 = Resistor [tolerance=±5% resistance=220 package=THT]
  LED1 = LED - 5mm [color="Red (633nm)" package="5 mm [THT]"]
  Q1 = NPN-Transistor [package="TO92 [THT]"]

nets:
  N1: Part1.A0, U1.connector6, R2.Pin_0
  N2: Part1.D12/MISO, R5.Pin_1
  N3: Part1.GND, U1.connector3, R3.Pin_1, R4.Pin_1, LED1.cathode
  N4: Part1.3V3, U1.connector7, R1.pin_0
  N5: Part1.5V, Q1.C
  N6: U1.connector4, R1.pin_1, R4.Pin_0
  N7: U1.connector5, R2.Pin_1, R3.Pin_0
  N8: R5.Pin_0, Q1.B
  N9: R6.Pin_0, Q1.E
  N10: R6.Pin_1, LED1.anode
