# Fritzing sketch yonubba (saved by Fritzing 0.9.3b)
breadboards: 1

parts:
  R1 = Resistor [tolerance=±5% resistance=560 package=THT]
  R2 = Resistor [tolerance=±5% resistance=560 package=THT]
  R3 = Resistor [tolerance=±5% resistance=560 package=THT]
  LED1 = RGB LED (com. cathode, rgb) [package="5 mm [THT]"]
  R4 = Photocell (LDR) [package=THT]
  R5 = Resistor [tolerance=±5% resistance=10k package=THT]
  Part1 = Arduino Mega 2560 (Rev3)

nets:
  N1: R1.Pin_0, Part1.D11_PWM
  N2: R1.Pin_1, LED1.red_anode
  N3: R2.Pin_0, Part1.D10_PWM
  N4: R2.Pin_1, LED1.green_anode
  N5: R3.Pin_0, Part1.D9_PWM
  N6: R3.Pin_1, LED1.blue_anode
  N7: LED1.common_cathode, R5.Pin_1, Part1.GND
  N8: R4.pin_0, R5.Pin_0, Part1.A0
  N9: R4.pin_1, Part1.3V3

notes:
  Tanner Helms
  RGB Circuit
  Tanner Helms
